// Logisim project jpu.circ as structural Verilog: 2 circuits, main circuit main
module main (
);

  wire clock_1_out, Dec_out, Inc_out, Load_out, Rst_out;
  wire [3:0] bit_extender_1_out;
  wire [31:0] reg_idls_1_output_value;

  reg_IDLS reg_idls_1 (
    .Load_value(32'h1), .Load(Load_out), .Decrement(Dec_out), .Increment(Inc_out), .Clock(clock_1_out),
    .Reset(Rst_out), .Output_value(reg_idls_1_output_value));
  Button Load (.out(Load_out));
  Button Dec (.out(Dec_out));
  Button Inc (.out(Inc_out));
  Clock clock_1 (.out(clock_1_out));
  Button Rst (.out(Rst_out));
  Bit_Extender #(.in_width(32), .out_width(4)) bit_extender_1 (.in(reg_idls_1_output_value), .out(bit_extender_1_out));
  Hex_Digit_Display hex_digit_display_1 (.value(bit_extender_1_out));  // open: dp
endmodule

module reg_IDLS (
  input  [31:0] Load_value,
  input  Clock,
  input  Reset,
  input  Load,
  input  Decrement,
  input  Increment,
  output [31:0] Output_value
);

  wire [1:0] priority_encoder_1_out;
  wire [31:0] adder_1_out, multiplexer_1_out, subtractor_1_out;

  Adder #(.width(32)) adder_1 (.a(32'h1), .b(Output_value), .out(adder_1_out));  // open: cin, cout
  Subtractor #(.width(32)) subtractor_1 (.a(Output_value), .b(32'h1), .out(subtractor_1_out));  // open: bin, bout
  Priority_Encoder #(.select(2)) priority_encoder_1 (
    .in0(Load), .in1(Decrement), .in2(Increment), .out(priority_encoder_1_out));  // open: in3, gs, en_out, en_in
  Multiplexer #(.select(2), .width(32)) multiplexer_1 (
    .in0(Load_value), .in1(subtractor_1_out), .in2(adder_1_out), .out(multiplexer_1_out),
    .sel(priority_encoder_1_out), .en(1'b1));  // open: in3
  Register #(.width(32)) register_1 (.D(multiplexer_1_out), .Q(Output_value), .clk(Clock), .clr(Reset));  // open: en
endmodule
